// Logisim project ALU.circ as structural Verilog: 1 circuit, main circuit ALU
module ALU (
  input  [15:0] in_1,
  input  [15:0] in_2,
  input  [15:0] in_3,
  input  [15:0] in_4,
  input  [15:0] in_5,
  input  [15:0] in_6,
  input  [15:0] in_7,
  input  [15:0] in_8,
  input  [15:0] in_9,
  input  [15:0] in_10,
  input  [15:0] in_11,
  input  [15:0] in_12,
  input  [15:0] in_13,
  input  [15:0] in_14,
  input  [15:0] in_15,
  output [15:0] out_16,
  output [15:0] out_17,
  output [15:0] out_18,
  output [15:0] out_19,
  output [15:0] out_20,
  output out_21,
  output out_22,
  output out_23,
  output [15:0] out_24,
  output [15:0] out_25
);

  wire [2:0] undriven_2;
  wire [3:0] bit_extender_1_out, bit_extender_2_out;
  wire [15:0] demultiplexer_1_out0, demultiplexer_1_out1, demultiplexer_1_out2, demultiplexer_1_out3,
       demultiplexer_1_out4, demultiplexer_1_out5, demultiplexer_1_out6, demultiplexer_1_out7, undriven;

  Demultiplexer #(.select(3), .width(16)) demultiplexer_1 (
    .out0(demultiplexer_1_out0), .out1(demultiplexer_1_out1), .out2(demultiplexer_1_out2),
    .out3(demultiplexer_1_out3), .out4(demultiplexer_1_out4), .out5(demultiplexer_1_out5),
    .out6(demultiplexer_1_out6), .out7(demultiplexer_1_out7), .in(undriven), .sel(undriven_2), .en(1'b1));
  Bit_Extender #(.in_width(16), .out_width(4)) bit_extender_1 (.in(in_13), .out(bit_extender_1_out));
  Bit_Extender #(.in_width(16), .out_width(4)) bit_extender_2 (.in(in_15), .out(bit_extender_2_out));
  Negator #(.width(16)) negator_1 (.in(in_1), .out(out_16));
  Adder #(.width(16)) adder_1 (.a(in_2), .b(in_3), .out(out_17));  // open: cin, cout
  Subtractor #(.width(16)) subtractor_1 (.a(in_4), .b(in_5), .out(out_18));  // open: bin, bout
  Multiplier #(.width(16)) multiplier_1 (.a(in_6), .b(in_7), .out(out_19));  // open: cin, cout
  Divider #(.width(16)) divider_1 (.a(in_8), .b(in_9), .out(out_20));  // open: upper, rem
  Comparator #(.width(16)) comparator_1 (.a(in_10), .b(in_11), .gt(out_21), .eq(out_22), .lt(out_23));
  Shifter #(.width(16)) shifter_1 (.in(in_12), .\dist (bit_extender_1_out), .out(out_24));
  Shifter #(.width(16), .shift("lr")) shifter_2 (.in(in_14), .\dist (bit_extender_2_out), .out(out_25));
endmodule
