// Logisim project Main bus.circ as structural Verilog: 1 circuit, main circuit Main bus
module Main_bus (
  input  [15:0] in_1,
  input  in_2,
  input  in_3,
  input  in_4,
  input  in_5,
  input  in_6,
  input  in_7,
  input  in_8,
  input  [2:0] in_9,
  input  in_10
);

  wire and_1_out, clk, IRBuf, MARBuf, PCBuf, PCEn, RAMRead;
  wire [3:0] Phase;
  wire [15:0] Accumulator_register_q, alu_1_p4, controlled_buffer_1_out, controlled_buffer_2_out,
       controlled_buffer_3_out, controlled_buffer_6_out, controlled_buffer_8_out, controlled_buffer_9_out,
       Input_register_2_q, Input_register_q, Instruction_register_q, Memory_access_register_q,
       Output_register_q, Program_counter_q, ram_1_data;

  Register #(.width(16)) Memory_access_register (
    .D(controlled_buffer_1_out), .en(1'b1), .Q(Memory_access_register_q), .clk(clk));  // open: clr
  Register #(.width(16)) Instruction_register (
    .D(controlled_buffer_2_out), .en(1'b1), .Q(Instruction_register_q), .clk(clk));  // open: clr
  Counter #(.width(4), .max('hf)) counter_1 (
    .count(1'b1), .Q(Phase), .clk(clk), .clr(and_1_out));  // open: load, D, carry
  and and_1 (and_1_out, Phase[3], ~Phase[2], Phase[1], ~Phase[0]);  // AND_Gate
  Counter #(.width(16), .max('hffff)) Program_counter (
    .count(PCEn), .Q(Program_counter_q), .clk(clk));  // open: load, D, carry, clr
  assign controlled_buffer_1_out = MARBuf ? controlled_buffer_3_out : 16'bz;  // Controlled_Buffer controlled_buffer_1
  RAM #(.addrWidth(16), .dataWidth(16)) ram_1 (
    .addr(Memory_access_register_q), .data(ram_1_data), .clk(clk), .ld(1'b1));  // open: sel, clr
  assign controlled_buffer_2_out = IRBuf ? controlled_buffer_3_out : 16'bz;  // Controlled_Buffer controlled_buffer_2
  ROM #(.addrWidth(4), .dataWidth(16)) rom_1 (.addr(Instruction_register_q[3:0]));  // open: data, sel
  assign controlled_buffer_3_out = in_4 ? Accumulator_register_q : 16'bz;  // Controlled_Buffer controlled_buffer_3
  assign controlled_buffer_3_out = PCBuf ? Program_counter_q : 16'bz;  // Controlled_Buffer controlled_buffer_4
  assign controlled_buffer_3_out = RAMRead ? ram_1_data : 16'bz;  // Controlled_Buffer controlled_buffer_5
  assign controlled_buffer_6_out = in_7 ? controlled_buffer_3_out : 16'bz;  // Controlled_Buffer controlled_buffer_6
  assign controlled_buffer_3_out = in_8 ? in_1 : 16'bz;  // Controlled_Buffer controlled_buffer_7
  assign controlled_buffer_8_out = in_5 ? controlled_buffer_3_out : 16'bz;  // Controlled_Buffer controlled_buffer_8
  assign controlled_buffer_9_out = in_6 ? controlled_buffer_3_out : 16'bz;  // Controlled_Buffer controlled_buffer_9
  Register #(.width(16)) Output_register (
    .D(controlled_buffer_6_out), .Q(Output_register_q), .clk(clk));  // open: en, clr
  Decoder #(.select(4)) decoder_1 (
    .out0(PCBuf), .out1(IRBuf), .out9(PCEn), .sel(Phase), .en(1'b1));  // open: out2, out3, out4, out5, out6, out7, out8, out10, out11, out12, out13, out14, out15
  Register #(.width(16)) Input_register (
    .D(controlled_buffer_8_out), .en(1'b1), .Q(Input_register_q), .clk(clk));  // open: clr
  Register #(.width(16)) Input_register_2 (
    .D(controlled_buffer_9_out), .en(1'b1), .Q(Input_register_2_q), .clk(clk));  // open: clr
  Hex_Digit_Display hex_digit_display_1 (.value(Output_register_q[15:12]));  // open: dp
  // ALU alu_1: pin names not known; wires that end beside it: Input_register_q, Input_register_2_q, in_9, alu_1_p4
  Hex_Digit_Display hex_digit_display_2 (.value(Output_register_q[11:8]));  // open: dp
  Hex_Digit_Display hex_digit_display_3 (.value(Output_register_q[7:4]));  // open: dp
  or or_1 (MARBuf, PCBuf, in_2);
  or or_2 (RAMRead, IRBuf, in_3);
  Clock clock_1 (.out(clk));
  Register #(.width(16)) Accumulator_register (
    .D(alu_1_p4), .en(1'b1), .Q(Accumulator_register_q), .clk(clk));  // open: clr
  Hex_Digit_Display hex_digit_display_4 (.value(Output_register_q[3:0]));  // open: dp

  // Other names for the same wires on the sheet: ALU[2:0] = in_9; ALUBuf = in_4; IBuf = in_8; OBuf = in_7;
  //   RegBufA = in_5; RegBufB = in_6

  // Notes on the sheet:
  //   PCEN
  //   ROM for control matrix
  //   PCBuf+MARBuf
  //   RAMBuf+IRBuf
  //   7 Stages of instruction
endmodule
