// Logisim project RAM.circ as structural Verilog: 3 circuits, main circuit RAM
module RAM (
  input  [3:0] Input,
  input  [1:0] Input_2,
  input  in_3,
  input  [3:0] Output
);

  wire decoder_1_out0, decoder_1_out1, decoder_1_out2, decoder_1_out3, memory_cell_1_output,
       memory_cell_2_output, memory_cell_3_output, memory_cell_4_output, memory_cell_5_output,
       memory_cell_6_output, memory_cell_7_output, memory_cell_8_output, memory_cell_9_output,
       memory_cell_10_output, memory_cell_11_output, memory_cell_12_output, memory_cell_13_output,
       memory_cell_14_output, memory_cell_15_output, memory_cell_16_output;

  Decoder #(.select(2), .disabled(0), .enable("false")) decoder_1 (
    .out0(decoder_1_out0), .out1(decoder_1_out1), .out2(decoder_1_out2), .out3(decoder_1_out3), .sel(Input_2));
  Memory_cell memory_cell_1 (.Select(decoder_1_out0), .Input(Input[3]), .Output(memory_cell_1_output), .R_W(in_3));
  Memory_cell memory_cell_2 (.Select(decoder_1_out1), .Input(Input[3]), .Output(memory_cell_2_output), .R_W(in_3));
  Memory_cell memory_cell_3 (.Select(decoder_1_out2), .Input(Input[3]), .Output(memory_cell_3_output), .R_W(in_3));
  Memory_cell memory_cell_4 (.Select(decoder_1_out3), .Input(Input[3]), .Output(memory_cell_4_output), .R_W(in_3));
  or or_1 (Output[3], memory_cell_1_output, memory_cell_2_output, memory_cell_3_output, memory_cell_4_output);
  Memory_cell memory_cell_5 (.Select(decoder_1_out0), .Input(Input[2]), .Output(memory_cell_5_output), .R_W(in_3));
  Memory_cell memory_cell_6 (.Select(decoder_1_out1), .Input(Input[2]), .Output(memory_cell_6_output), .R_W(in_3));
  Memory_cell memory_cell_7 (.Select(decoder_1_out2), .Input(Input[2]), .Output(memory_cell_7_output), .R_W(in_3));
  Memory_cell memory_cell_8 (.Select(decoder_1_out3), .Input(Input[2]), .Output(memory_cell_8_output), .R_W(in_3));
  or or_2 (Output[2], memory_cell_5_output, memory_cell_6_output, memory_cell_7_output, memory_cell_8_output);
  Memory_cell memory_cell_9 (.Select(decoder_1_out0), .Input(Input[1]), .Output(memory_cell_9_output), .R_W(in_3));
  Memory_cell memory_cell_10 (.Select(decoder_1_out1), .Input(Input[1]), .Output(memory_cell_10_output), .R_W(in_3));
  Memory_cell memory_cell_11 (.Select(decoder_1_out2), .Input(Input[1]), .Output(memory_cell_11_output), .R_W(in_3));
  Memory_cell memory_cell_12 (.Select(decoder_1_out3), .Input(Input[1]), .Output(memory_cell_12_output), .R_W(in_3));
  or or_3 (Output[1], memory_cell_9_output, memory_cell_10_output, memory_cell_11_output, memory_cell_12_output);
  Memory_cell memory_cell_13 (.Select(decoder_1_out0), .Input(Input[0]), .Output(memory_cell_13_output), .R_W(in_3));
  Memory_cell memory_cell_14 (.Select(decoder_1_out1), .Input(Input[0]), .Output(memory_cell_14_output), .R_W(in_3));
  Memory_cell memory_cell_15 (.Select(decoder_1_out2), .Input(Input[0]), .Output(memory_cell_15_output), .R_W(in_3));
  Memory_cell memory_cell_16 (.Select(decoder_1_out3), .Input(Input[0]), .Output(memory_cell_16_output), .R_W(in_3));
  or or_4 (Output[0], memory_cell_13_output, memory_cell_14_output, memory_cell_15_output, memory_cell_16_output);
endmodule

module Memory_cell (
  input  Select,
  input  Input,
  input  R_W,
  output Output
);

  wire and_1_out, and_2_out, not_1_out, not_2_out, sr_latch_1_output;

  not not_1 (not_1_out, Input);
  and and_1 (and_1_out, Select, not_2_out, Input);
  and and_2 (and_2_out, Select, not_2_out, not_1_out);
  not not_2 (not_2_out, R_W);
  SR_latch sr_latch_1 (.Set(and_1_out), .Reset(and_2_out), .Output(sr_latch_1_output));
  and and_3 (Output, Select, sr_latch_1_output, R_W);
endmodule

module SR_latch (
  input  Set,
  input  Reset,
  output Output
);

  wire nor_2_out;

  nor nor_1 (Output, Set, nor_2_out);
  nor nor_2 (nor_2_out, Output, Reset);
endmodule
